// Logisim project DD_signed_multiplier.circ as structural Verilog: 13 circuits, main circuit main
module main (
  input  [7:0] multiplier,
  input  [7:0] multiplicand,
  output [14:0] out_3,
  output [1:0] out_4
);

  wire clock_1_out, clockdivider_1_out_2, decoder_1_out1, decoder_1_out2, decoder_1_out3, leftButton_out,
       multiply_out, multiplypart2_1_endmult, multiplypart2_1_sign, rightButton_out;
  wire [1:0] counter_1_q;
  wire [3:0] bcd_to_7_segment_decoder_2_p1, bcd_to_7_segment_decoder_3_p1, bcd_to_7_segment_decoder_4_p1,
       binarytobcd_1_digit_1, binarytobcd_1_digit_2, binarytobcd_1_digit_3, binarytobcd_1_digit_4,
       binarytobcd_1_digit_5, multiplexer_1_out, multiplexer_2_out, multiplexer_3_out, multiplexer_4_out,
       multiplexer_5_out;

  Clock clock_1 (.out(clock_1_out));
  Button multiply (.out(multiply_out));
  clockDivider clockdivider_1 (.clk(clock_1_out), .out_2(clockdivider_1_out_2));
  Counter #(.max('h3), .width(2)) counter_1 (
    .count(1'b1), .clk(clockdivider_1_out_2), .Q(counter_1_q));  // open: clr, load, up, D, carry
  multiplypart2 multiplypart2_1 (
    .Multiplier(multiplicand), .Multiplicand(multiplier), .MultButton(multiply_out), .clk(clock_1_out),
    .Sign(multiplypart2_1_sign), .EndMult(multiplypart2_1_endmult), .Product(out_3));
  LED led_1 (.in(multiplypart2_1_endmult));
  Button rightButton (.out(rightButton_out));
  Button leftButton (.out(leftButton_out));
  binarytoBCD binarytobcd_1 (
    .in_1(out_3), .Digit_1(binarytobcd_1_digit_1), .Digit_2(binarytobcd_1_digit_2),
    .Digit_3(binarytobcd_1_digit_3), .Digit_4(binarytobcd_1_digit_4), .Digit_5(binarytobcd_1_digit_5));
  Multiplexer #(.width(4)) multiplexer_1 (
    .in0(4'b1010), .in1(4'b1011), .out(multiplexer_1_out), .sel(multiplypart2_1_sign));
  Multiplexer #(.select(2), .width(4)) multiplexer_2 (
    .in0(binarytobcd_1_digit_1), .in1(binarytobcd_1_digit_2), .in2(binarytobcd_1_digit_3),
    .in3(binarytobcd_1_digit_3), .out(multiplexer_2_out), .sel(out_4));
  Multiplexer #(.select(2), .width(4)) multiplexer_3 (
    .in0(binarytobcd_1_digit_2), .in1(binarytobcd_1_digit_3), .in2(binarytobcd_1_digit_4),
    .in3(binarytobcd_1_digit_4), .out(multiplexer_3_out), .sel(out_4));
  Multiplexer #(.select(2), .width(4)) multiplexer_4 (
    .in0(binarytobcd_1_digit_3), .in1(binarytobcd_1_digit_4), .in2(binarytobcd_1_digit_5),
    .in3(binarytobcd_1_digit_5), .out(multiplexer_4_out), .sel(out_4));
  buttonControlUnit buttoncontrolunit_1 (
    .rightButton(rightButton_out), .leftButton(leftButton_out), .multiplyButton(multiply_out),
    .clk(clock_1_out), .out_5(out_4));
  Multiplexer #(.select(2), .width(4)) multiplexer_5 (
    .in0(multiplexer_1_out), .in1(multiplexer_2_out), .in2(multiplexer_3_out), .in3(multiplexer_4_out),
    .out(multiplexer_5_out), .sel(counter_1_q));
  Decoder #(.select(2)) decoder_1 (
    .out1(decoder_1_out1), .out2(decoder_1_out2), .out3(decoder_1_out3), .sel(counter_1_q), .en(1'b1));  // open: out0
  _7_Segment_Display u_7_segment_display_1 (.g(multiplypart2_1_sign));  // open: f, a, b, e, d, c, dp
  // BCD_to_7_Segment_decoder bcd_to_7_segment_decoder_1: pin names not known
  _7_Segment_Display u_7_segment_display_2 ();  // open: g, f, a, b, e, d, c, dp
  // BCD_to_7_Segment_decoder bcd_to_7_segment_decoder_2: pin names not known; wires that end beside it: bcd_to_7_segment_decoder_2_p1
  Multiplexer #(.width(4)) multiplexer_6 (
    .in0(4'b1010), .in1(multiplexer_5_out), .out(bcd_to_7_segment_decoder_2_p1), .sel(decoder_1_out1));
  _7_Segment_Display u_7_segment_display_3 ();  // open: g, f, a, b, e, d, c, dp
  // BCD_to_7_Segment_decoder bcd_to_7_segment_decoder_3: pin names not known; wires that end beside it: bcd_to_7_segment_decoder_3_p1
  _7_Segment_Display u_7_segment_display_4 ();  // open: g, f, a, b, e, d, c, dp
  // BCD_to_7_Segment_decoder bcd_to_7_segment_decoder_4: pin names not known; wires that end beside it: bcd_to_7_segment_decoder_4_p1
  Multiplexer #(.width(4)) multiplexer_7 (
    .in0(4'b1010), .in1(multiplexer_5_out), .out(bcd_to_7_segment_decoder_3_p1), .sel(decoder_1_out2));
  Multiplexer #(.width(4)) multiplexer_8 (
    .in0(4'b1010), .in1(multiplexer_5_out), .out(bcd_to_7_segment_decoder_4_p1), .sel(decoder_1_out3));

  // Notes on the sheet:
  //   positve
  //   negative
endmodule

module buttonDetector (
  input  Button,
  output out_2
);

  wire and_1_out, clock_1_out, d_ff_1_q, d_ff_2_q, d_ff_3_q, d_ff_4_q, d_ff_5_q, d_ff_6_q, d_ff_6_qn;

  Clock clock_1 (.out(clock_1_out));
  D_Flip_Flop d_ff_1 (.D(Button), .clk(clock_1_out), .Q(d_ff_1_q));  // open: Qn, preset, reset
  D_Flip_Flop d_ff_2 (.D(d_ff_1_q), .clk(clock_1_out), .Q(d_ff_2_q));  // open: Qn, preset, reset
  D_Flip_Flop d_ff_3 (.D(d_ff_2_q), .clk(clock_1_out), .Q(d_ff_3_q));  // open: Qn, preset, reset
  and and_1 (and_1_out, d_ff_1_q, d_ff_2_q, d_ff_3_q);
  D_Flip_Flop d_ff_4 (.D(and_1_out), .clk(clock_1_out), .Q(d_ff_4_q));  // open: Qn, preset, reset
  D_Flip_Flop d_ff_5 (.D(d_ff_4_q), .clk(clock_1_out), .Q(d_ff_5_q));  // open: Qn, preset, reset
  D_Flip_Flop d_ff_6 (.D(d_ff_5_q), .clk(clock_1_out), .Q(d_ff_6_q), .Qn(d_ff_6_qn));  // open: preset, reset
  and and_2 (out_2, d_ff_5_q, d_ff_6_qn);

  // Notes on the sheet:
  //   debouncer
  //   synchronizer
  //   rising edge detector
endmodule

module unsignedMultiplier (
  input  rst,
  input  [7:0] multiplier,
  input  [7:0] multiplicand,
  input  multButton,
  output [14:0] product,
  output sign
);

  wire buttondetector_1_out_2, clock_1_out, d_ff_1_q, nand_1_out, not_1_out, not_2_out, not_3_out, not_4_out,
       or_1_out, shift_register_1_p3, shift_register_1_p12, t_ff_1_q, undriven, xor_1_out, xor_2_out;
  wire [3:0] counter_1_q;
  wire [7:0] multiplexer_1_out, multiplexer_2_out, shift_register_2_p22, twoscomplement_1_out_2,
       twoscomplement_2_out_2;
  wire [14:0] adder_1_out, multiplexer_3_out, register_1_q, shift_register_2_p23;

  Clock clock_1 (.out(clock_1_out));
  Button button_1 ();  // open: out
  D_Flip_Flop d_ff_1 (.D(buttondetector_1_out_2), .clk(clock_1_out), .Q(d_ff_1_q));  // open: Qn, preset, reset
  buttonDetector buttondetector_1 (.Button(multButton), .out_2(buttondetector_1_out_2));
  or or_1 (or_1_out, buttondetector_1_out_2, not_4_out);
  T_Flip_Flop t_ff_1 (.T(or_1_out), .clk(clock_1_out), .Q(t_ff_1_q));  // open: Qn, reset, preset
  twosComplement twoscomplement_1 (.in_1(multiplier), .out_2(twoscomplement_1_out_2));
  twosComplement twoscomplement_2 (.in_1(multiplicand), .out_2(twoscomplement_2_out_2));
  Counter #(.max('h8), .width(4)) counter_1 (
    .clr(undriven), .count(t_ff_1_q), .clk(clock_1_out), .Q(counter_1_q));  // open: load, up, D, carry
  Multiplexer #(.width(8)) multiplexer_1 (
    .in0(twoscomplement_1_out_2), .in1(multiplier), .out(multiplexer_1_out), .sel(xor_1_out));
  xor xor_1 (xor_1_out, multiplier[7], 1'b1);
  xor xor_2 (xor_2_out, multiplicand[7], 1'b1);
  Multiplexer #(.width(8)) multiplexer_2 (
    .in0(twoscomplement_2_out_2), .in1(multiplicand), .out(multiplexer_2_out), .sel(xor_2_out));
  xor xor_3 (sign, multiplicand[7], multiplier[7]);
  not not_1 (not_1_out, counter_1_q[0]);
  not not_2 (not_2_out, counter_1_q[1]);
  not not_3 (not_3_out, counter_1_q[2]);
  // Shift_Register shift_register_1: pin names not known; wires that end beside it: rst, d_ff_1_q, shift_register_1_p3, clock_1_out, 1'b0, multiplexer_1_out[7], multiplexer_1_out[6], multiplexer_1_out[5], multiplexer_1_out[4], multiplexer_1_out[3], multiplexer_1_out[2], shift_register_1_p12, shift_register_1_p12, shift_register_2_p22[7], shift_register_2_p22[6], shift_register_2_p22[5], shift_register_2_p22[4], shift_register_2_p22[3]
  // Shift_Register #(.length(15)) shift_register_2: pin names not known; wires that end beside it: multiplexer_1_out[1], multiplexer_1_out[0], rst, d_ff_1_q, shift_register_1_p3, clock_1_out, 1'b0, multiplexer_2_out[0], multiplexer_2_out[1], multiplexer_2_out[2], multiplexer_2_out[3], multiplexer_2_out[4], multiplexer_2_out[5], multiplexer_2_out[6], multiplexer_2_out[7], 1'b0, 1'b0, 1'b0, 1'b0, shift_register_2_p22[2], shift_register_2_p22[1], shift_register_2_p22[0], shift_register_2_p23[0], shift_register_2_p23[1], shift_register_2_p23[2], shift_register_2_p23[3], shift_register_2_p23[4], shift_register_2_p23[5], shift_register_2_p23[6], shift_register_2_p23[7], shift_register_2_p23[8], shift_register_2_p23[9], shift_register_2_p23[10], shift_register_2_p23[11]
  nand nand_1 (nand_1_out, not_1_out, not_2_out, not_3_out, counter_1_q[3]);
  not not_4 (not_4_out, nand_1_out);
  and and_1 (shift_register_1_p3, t_ff_1_q, nand_1_out);
  Adder #(.width(15)) adder_1 (.a(multiplexer_3_out), .b(register_1_q), .out(adder_1_out), .cin(1'b0));  // open: cout
  Multiplexer #(.width(15)) multiplexer_3 (
    .in0({15{1'b0}}), .in1(shift_register_2_p23), .out(multiplexer_3_out), .sel(shift_register_2_p22[0]));
  Register #(.width(15)) register_1 (
    .D(adder_1_out), .en(shift_register_1_p3), .clk(clock_1_out), .Q(register_1_q),
    .clr(buttondetector_1_out_2));
  Multiplexer #(.width(15)) multiplexer_4 (
    .in0(register_1_q), .in1({15{1'b0}}), .out(product), .sel(shift_register_1_p3));
endmodule

module buttonControlUnit (
  input  rightButton,
  input  leftButton,
  input  multiplyButton,
  input  clk,
  output [1:0] out_5
);

  wire and_1_out, and_2_out, buttondetector_1_out_2, buttondetector_2_out_2, buttondetector_3_out_2,
       nand_1_out, nand_2_out, not_1_out, not_2_out, or_1_out;

  buttonDetector buttondetector_1 (.Button(rightButton), .out_2(buttondetector_1_out_2));
  and and_1 (and_1_out, buttondetector_1_out_2, nand_1_out);
  nand nand_1 (nand_1_out, out_5[1], not_2_out);
  buttonDetector buttondetector_2 (.Button(multiplyButton), .out_2(buttondetector_2_out_2));
  and and_2 (and_2_out, buttondetector_3_out_2, nand_2_out);
  or or_1 (or_1_out, and_1_out, and_2_out);
  buttonDetector buttondetector_3 (.Button(leftButton), .out_2(buttondetector_3_out_2));
  Counter #(.max('h3), .width(2)) counter_1 (
    .load(buttondetector_2_out_2), .up(buttondetector_1_out_2), .count(or_1_out), .clk(clk), .D(2'b00),
    .Q(out_5));  // open: clr, carry
  nand nand_2 (nand_2_out, not_1_out, not_2_out);
  not not_1 (not_1_out, out_5[1]);
  not not_2 (not_2_out, out_5[0]);
endmodule

module clockDivider (
  input  clk,
  output out_2
);

  wire [2:0] counter_1_q;

  Counter #(.max('h7), .width(3)) counter_1 (
    .load(counter_1_q[2]), .count(1'b1), .clk(clk), .D(3'b000), .Q(counter_1_q));  // open: clr, up, carry
  T_Flip_Flop t_ff_1 (.T(counter_1_q[2]), .clk(clk), .Q(out_2));  // open: Qn, reset, preset
endmodule

module binarytoBCD (
  input  [14:0] in_1,
  output [3:0] Digit_1,
  output [3:0] Digit_2,
  output [3:0] Digit_3,
  output [3:0] Digit_4,
  output [3:0] Digit_5
);

  wire shift_add_3_1_s0, shift_add_3_1_s1, shift_add_3_1_s2, shift_add_3_1_s3, shift_add_3_2_s0,
       shift_add_3_2_s1, shift_add_3_2_s2, shift_add_3_3_s0, shift_add_3_3_s1, shift_add_3_3_s2,
       shift_add_3_5_s0, shift_add_3_5_s1, shift_add_3_5_s2, shift_add_3_5_s3, shift_add_3_6_s0,
       shift_add_3_6_s1, shift_add_3_6_s2, shift_add_3_6_s3, shift_add_3_7_s0, shift_add_3_7_s1,
       shift_add_3_7_s2, shift_add_3_7_s3, shift_add_3_8_s0, shift_add_3_8_s1, shift_add_3_8_s2,
       shift_add_3_8_s3, shift_add_3_9_s0, shift_add_3_9_s1, shift_add_3_9_s2, shift_add_3_9_s3,
       shift_add_3_10_s0, shift_add_3_10_s1, shift_add_3_10_s2, shift_add_3_10_s3, shift_add_3_11_s0,
       shift_add_3_11_s1, shift_add_3_11_s2, shift_add_3_11_s3, shift_add_3_12_s0, shift_add_3_12_s1,
       shift_add_3_12_s2, shift_add_3_12_s3, shift_add_3_13_s0, shift_add_3_13_s1, shift_add_3_13_s2,
       shift_add_3_13_s3, shift_add_3_14_s0, shift_add_3_14_s1, shift_add_3_14_s2, shift_add_3_14_s3,
       shift_add_3_15_s0, shift_add_3_15_s1, shift_add_3_15_s2, shift_add_3_15_s3, shift_add_3_16_s0,
       shift_add_3_16_s1, shift_add_3_16_s2, shift_add_3_16_s3, shift_add_3_17_s0, shift_add_3_17_s1,
       shift_add_3_17_s2, shift_add_3_17_s3, shift_add_3_19_s0, shift_add_3_19_s1, shift_add_3_19_s2,
       shift_add_3_19_s3, shift_add_3_20_s0, shift_add_3_20_s1, shift_add_3_20_s2, shift_add_3_20_s3,
       shift_add_3_21_s0, shift_add_3_21_s1, shift_add_3_21_s2, shift_add_3_21_s3, shift_add_3_22_s0,
       shift_add_3_22_s1, shift_add_3_22_s2, shift_add_3_22_s3, shift_add_3_23_s0, shift_add_3_23_s1,
       shift_add_3_23_s2, shift_add_3_23_s3, shift_add_3_24_s0, shift_add_3_24_s1, shift_add_3_24_s2,
       shift_add_3_24_s3, shift_add_3_26_s0, shift_add_3_26_s1, shift_add_3_26_s2, shift_add_3_26_s3,
       shift_add_3_27_s0, shift_add_3_27_s1, shift_add_3_27_s2, shift_add_3_27_s3, shift_add_3_28_s0,
       shift_add_3_28_s1, shift_add_3_28_s2, shift_add_3_28_s3, shift_add_3_29_s0, shift_add_3_29_s1,
       shift_add_3_29_s2, shift_add_3_29_s3;

  Shift_Add_3 shift_add_3_1 (
    .b0(shift_add_3_14_s3), .b1(shift_add_3_6_s3), .b2(shift_add_3_5_s3), .b3(1'b0), .S0(shift_add_3_1_s0),
    .S1(shift_add_3_1_s1), .S2(shift_add_3_1_s2), .S3(shift_add_3_1_s3));
  Shift_Add_3 shift_add_3_2 (
    .b0(shift_add_3_8_s3), .b1(shift_add_3_7_s3), .b2(shift_add_3_1_s3), .b3(1'b0), .S0(shift_add_3_2_s0),
    .S1(shift_add_3_2_s1), .S2(shift_add_3_2_s2), .S3(Digit_1[2]));
  Shift_Add_3 shift_add_3_3 (
    .b0(shift_add_3_9_s3), .b1(shift_add_3_2_s0), .b2(shift_add_3_2_s1), .b3(shift_add_3_2_s2),
    .S0(shift_add_3_3_s0), .S1(shift_add_3_3_s1), .S2(shift_add_3_3_s2), .S3(Digit_1[1]));
  Shift_Add_3 shift_add_3_4 (
    .b0(shift_add_3_10_s3), .b1(shift_add_3_3_s0), .b2(shift_add_3_3_s1), .b3(shift_add_3_3_s2),
    .S0(Digit_2[1]), .S1(Digit_2[2]), .S2(Digit_2[3]), .S3(Digit_1[0]));
  Shift_Add_3 shift_add_3_5 (
    .b0(shift_add_3_13_s3), .b1(shift_add_3_12_s3), .b2(shift_add_3_11_s3), .b3(1'b0), .S0(shift_add_3_5_s0),
    .S1(shift_add_3_5_s1), .S2(shift_add_3_5_s2), .S3(shift_add_3_5_s3));
  Shift_Add_3 shift_add_3_6 (
    .b0(shift_add_3_19_s3), .b1(shift_add_3_5_s0), .b2(shift_add_3_5_s1), .b3(shift_add_3_5_s2),
    .S0(shift_add_3_6_s0), .S1(shift_add_3_6_s1), .S2(shift_add_3_6_s2), .S3(shift_add_3_6_s3));
  Shift_Add_3 shift_add_3_7 (
    .b0(shift_add_3_15_s3), .b1(shift_add_3_1_s0), .b2(shift_add_3_1_s1), .b3(shift_add_3_1_s2),
    .S0(shift_add_3_7_s0), .S1(shift_add_3_7_s1), .S2(shift_add_3_7_s2), .S3(shift_add_3_7_s3));
  Shift_Add_3 shift_add_3_8 (
    .b0(shift_add_3_16_s3), .b1(shift_add_3_7_s0), .b2(shift_add_3_7_s1), .b3(shift_add_3_7_s2),
    .S0(shift_add_3_8_s0), .S1(shift_add_3_8_s1), .S2(shift_add_3_8_s2), .S3(shift_add_3_8_s3));
  Shift_Add_3 shift_add_3_9 (
    .b0(shift_add_3_17_s3), .b1(shift_add_3_8_s0), .b2(shift_add_3_8_s1), .b3(shift_add_3_8_s2),
    .S0(shift_add_3_9_s0), .S1(shift_add_3_9_s1), .S2(shift_add_3_9_s2), .S3(shift_add_3_9_s3));
  Shift_Add_3 shift_add_3_10 (
    .b0(shift_add_3_23_s3), .b1(shift_add_3_9_s0), .b2(shift_add_3_9_s1), .b3(shift_add_3_9_s2),
    .S0(shift_add_3_10_s0), .S1(shift_add_3_10_s1), .S2(shift_add_3_10_s2), .S3(shift_add_3_10_s3));
  Shift_Add_3 shift_add_3_11 (
    .b0(in_1[12]), .b1(in_1[13]), .b2(in_1[14]), .b3(1'b0), .S0(shift_add_3_11_s0), .S1(shift_add_3_11_s1),
    .S2(shift_add_3_11_s2), .S3(shift_add_3_11_s3));
  Shift_Add_3 shift_add_3_12 (
    .b0(in_1[11]), .b1(shift_add_3_11_s0), .b2(shift_add_3_11_s1), .b3(shift_add_3_11_s2),
    .S0(shift_add_3_12_s0), .S1(shift_add_3_12_s1), .S2(shift_add_3_12_s2), .S3(shift_add_3_12_s3));
  Shift_Add_3 shift_add_3_13 (
    .b0(in_1[10]), .b1(shift_add_3_12_s0), .b2(shift_add_3_12_s1), .b3(shift_add_3_12_s2),
    .S0(shift_add_3_13_s0), .S1(shift_add_3_13_s1), .S2(shift_add_3_13_s2), .S3(shift_add_3_13_s3));
  Shift_Add_3 shift_add_3_14 (
    .b0(shift_add_3_20_s3), .b1(shift_add_3_6_s0), .b2(shift_add_3_6_s1), .b3(shift_add_3_6_s2),
    .S0(shift_add_3_14_s0), .S1(shift_add_3_14_s1), .S2(shift_add_3_14_s2), .S3(shift_add_3_14_s3));
  Shift_Add_3 shift_add_3_15 (
    .b0(shift_add_3_21_s3), .b1(shift_add_3_14_s0), .b2(shift_add_3_14_s1), .b3(shift_add_3_14_s2),
    .S0(shift_add_3_15_s0), .S1(shift_add_3_15_s1), .S2(shift_add_3_15_s2), .S3(shift_add_3_15_s3));
  Shift_Add_3 shift_add_3_16 (
    .b0(shift_add_3_22_s3), .b1(shift_add_3_15_s0), .b2(shift_add_3_15_s1), .b3(shift_add_3_15_s2),
    .S0(shift_add_3_16_s0), .S1(shift_add_3_16_s1), .S2(shift_add_3_16_s2), .S3(shift_add_3_16_s3));
  Shift_Add_3 shift_add_3_17 (
    .b0(shift_add_3_26_s3), .b1(shift_add_3_16_s0), .b2(shift_add_3_16_s1), .b3(shift_add_3_16_s2),
    .S0(shift_add_3_17_s0), .S1(shift_add_3_17_s1), .S2(shift_add_3_17_s2), .S3(shift_add_3_17_s3));
  Shift_Add_3 shift_add_3_18 (
    .b0(shift_add_3_24_s3), .b1(shift_add_3_10_s0), .b2(shift_add_3_10_s1), .b3(shift_add_3_10_s2),
    .S0(Digit_3[1]), .S1(Digit_3[2]), .S2(Digit_3[3]), .S3(Digit_2[0]));
  Shift_Add_3 shift_add_3_19 (
    .b0(in_1[9]), .b1(shift_add_3_13_s0), .b2(shift_add_3_13_s1), .b3(shift_add_3_13_s2),
    .S0(shift_add_3_19_s0), .S1(shift_add_3_19_s1), .S2(shift_add_3_19_s2), .S3(shift_add_3_19_s3));
  Shift_Add_3 shift_add_3_20 (
    .b0(in_1[8]), .b1(shift_add_3_19_s0), .b2(shift_add_3_19_s1), .b3(shift_add_3_19_s2),
    .S0(shift_add_3_20_s0), .S1(shift_add_3_20_s1), .S2(shift_add_3_20_s2), .S3(shift_add_3_20_s3));
  Shift_Add_3 shift_add_3_21 (
    .b0(in_1[7]), .b1(shift_add_3_20_s0), .b2(shift_add_3_20_s1), .b3(shift_add_3_20_s2),
    .S0(shift_add_3_21_s0), .S1(shift_add_3_21_s1), .S2(shift_add_3_21_s2), .S3(shift_add_3_21_s3));
  Shift_Add_3 shift_add_3_22 (
    .b0(in_1[6]), .b1(shift_add_3_21_s0), .b2(shift_add_3_21_s1), .b3(shift_add_3_21_s2),
    .S0(shift_add_3_22_s0), .S1(shift_add_3_22_s1), .S2(shift_add_3_22_s2), .S3(shift_add_3_22_s3));
  Shift_Add_3 shift_add_3_23 (
    .b0(shift_add_3_27_s3), .b1(shift_add_3_17_s0), .b2(shift_add_3_17_s1), .b3(shift_add_3_17_s2),
    .S0(shift_add_3_23_s0), .S1(shift_add_3_23_s1), .S2(shift_add_3_23_s2), .S3(shift_add_3_23_s3));
  Shift_Add_3 shift_add_3_24 (
    .b0(shift_add_3_28_s3), .b1(shift_add_3_23_s0), .b2(shift_add_3_23_s1), .b3(shift_add_3_23_s2),
    .S0(shift_add_3_24_s0), .S1(shift_add_3_24_s1), .S2(shift_add_3_24_s2), .S3(shift_add_3_24_s3));
  Shift_Add_3 shift_add_3_25 (
    .b0(shift_add_3_29_s3), .b1(shift_add_3_24_s0), .b2(shift_add_3_24_s1), .b3(shift_add_3_24_s2),
    .S0(Digit_4[1]), .S1(Digit_4[2]), .S2(Digit_4[3]), .S3(Digit_3[0]));
  Shift_Add_3 shift_add_3_26 (
    .b0(in_1[5]), .b1(shift_add_3_22_s0), .b2(shift_add_3_22_s1), .b3(shift_add_3_22_s2),
    .S0(shift_add_3_26_s0), .S1(shift_add_3_26_s1), .S2(shift_add_3_26_s2), .S3(shift_add_3_26_s3));
  Shift_Add_3 shift_add_3_27 (
    .b0(in_1[4]), .b1(shift_add_3_26_s0), .b2(shift_add_3_26_s1), .b3(shift_add_3_26_s2),
    .S0(shift_add_3_27_s0), .S1(shift_add_3_27_s1), .S2(shift_add_3_27_s2), .S3(shift_add_3_27_s3));
  Shift_Add_3 shift_add_3_28 (
    .b0(in_1[3]), .b1(shift_add_3_27_s0), .b2(shift_add_3_27_s1), .b3(shift_add_3_27_s2),
    .S0(shift_add_3_28_s0), .S1(shift_add_3_28_s1), .S2(shift_add_3_28_s2), .S3(shift_add_3_28_s3));
  Shift_Add_3 shift_add_3_29 (
    .b0(in_1[2]), .b1(shift_add_3_28_s0), .b2(shift_add_3_28_s1), .b3(shift_add_3_28_s2),
    .S0(shift_add_3_29_s0), .S1(shift_add_3_29_s1), .S2(shift_add_3_29_s2), .S3(shift_add_3_29_s3));
  Shift_Add_3 shift_add_3_30 (
    .b0(in_1[1]), .b1(shift_add_3_29_s0), .b2(shift_add_3_29_s1), .b3(shift_add_3_29_s2), .S0(Digit_5[1]),
    .S1(Digit_5[2]), .S2(Digit_5[3]), .S3(Digit_4[0]));

  assign Digit_1[3] = 1'b0;
  assign Digit_5[0] = in_1[0];
endmodule

module twosComplement (
  input  [7:0] in_1,
  output [7:0] out_2
);

  wire adder_1_cout, adder_2_cout, adder_3_cout, adder_4_cout, adder_5_cout, adder_6_cout;

  Adder #(.width(1)) adder_1 (.a(in_1[1]), .b(in_1[0]), .out(out_2[1]), .cin(1'b0), .cout(adder_1_cout));
  Adder #(.width(1)) adder_2 (.a(out_2[1]), .b(adder_1_cout), .out(out_2[2]), .cin(in_1[2]), .cout(adder_2_cout));
  Adder #(.width(1)) adder_3 (.a(out_2[2]), .b(adder_2_cout), .out(out_2[3]), .cin(in_1[3]), .cout(adder_3_cout));
  Adder #(.width(1)) adder_4 (.a(out_2[3]), .b(adder_3_cout), .out(out_2[4]), .cin(in_1[4]), .cout(adder_4_cout));
  Adder #(.width(1)) adder_5 (.a(out_2[4]), .b(adder_4_cout), .out(out_2[5]), .cin(in_1[5]), .cout(adder_5_cout));
  Adder #(.width(1)) adder_6 (.a(out_2[5]), .b(adder_5_cout), .out(out_2[6]), .cin(in_1[6]), .cout(adder_6_cout));
  Adder #(.width(1)) adder_7 (.a(out_2[6]), .b(adder_6_cout), .out(out_2[7]), .cin(in_1[7]));  // open: cout

  assign out_2[0] = in_1[0];

  // Notes on the sheet:
  //   in_1: initial=0x6
endmodule

module Shift_Add_3 (
  input  b0,
  input  b1,
  input  b2,
  input  b3,
  output S0,
  output S1,
  output S2,
  output S3
);

  S0_circuit s0_circuit_1 (.A(b3), .B(b2), .C(b1), .D(b0), .S0(S0));
  S1_circuit s1_circuit_1 (.A(b3), .B(b2), .C(b1), .D(b0), .S1(S1));
  S2_circuit s2_circuit_1 (.A(b3), .B(b2), .C(b1), .D(b0), .S2(S2));
  S3_circuit s3_circuit_1 (.A(b3), .B(b2), .C(b1), .D(b0), .S3(S3));
endmodule

module S0_circuit (
  input  A,
  input  B,
  input  C,
  input  D,
  output S0
);

  wire and_1_out, and_2_out, and_3_out, not_1_out, not_2_out, not_3_out;

  not not_1 (not_1_out, A);
  not not_2 (not_2_out, B);
  not not_3 (not_3_out, D);
  and and_1 (and_1_out, A, not_3_out);
  and and_2 (and_2_out, not_1_out, not_2_out, D);
  and and_3 (and_3_out, B, C, not_3_out);
  or or_1 (S0, and_1_out, and_2_out, and_3_out);
endmodule

module S1_circuit (
  input  A,
  input  B,
  input  C,
  input  D,
  output S1
);

  wire and_1_out, and_2_out, and_3_out, not_1_out, not_2_out;

  not not_1 (not_1_out, B);
  not not_2 (not_2_out, D);
  and and_1 (and_1_out, not_1_out, C);
  and and_2 (and_2_out, C, D);
  and and_3 (and_3_out, A, not_2_out);
  or or_1 (S1, and_1_out, and_2_out, and_3_out);
endmodule

module S2_circuit (
  input  A,
  input  B,
  input  C,
  input  D,
  output S2
);

  wire and_1_out, and_2_out, not_1_out, not_2_out;

  not not_1 (not_1_out, C);
  not not_2 (not_2_out, D);
  and and_1 (and_1_out, A, D);
  and and_2 (and_2_out, B, not_1_out, not_2_out);
  or or_1 (S2, and_1_out, and_2_out);
endmodule

module S3_circuit (
  input  A,
  input  B,
  input  C,
  input  D,
  output S3
);

  wire and_1_out, and_2_out;

  and and_1 (and_1_out, B, D);
  and and_2 (and_2_out, B, C);
  or or_1 (S3, A, and_1_out, and_2_out);
endmodule

module multiplypart2 (
  input  [7:0] Multiplier,
  input  [7:0] Multiplicand,
  input  MultButton,
  input  clk,
  output Sign,
  output EndMult,
  output [14:0] Product
);

  wire buttondetector_1_out_2, shift_register_1_p1, shift_register_1_p5, shift_register_1_p14,
       shift_register_1_p16, shift_register_1_p17, shift_register_1_p18, shift_register_1_p19,
       shift_register_1_p20, shift_register_2_p16, shift_register_2_p17, shift_register_2_p18;
  wire [7:0] multiplexer_1_out, multiplexer_2_out, twoscomplement_1_out_2, twoscomplement_2_out_2;
  wire [14:0] adder_1_out, multiplexer_3_out, register_1_q, shift_register_2_p19;

  twosComplement twoscomplement_1 (.in_1(Multiplier), .out_2(twoscomplement_1_out_2));
  twosComplement twoscomplement_2 (.in_1(Multiplicand), .out_2(twoscomplement_2_out_2));
  buttonDetector buttondetector_1 (.Button(MultButton), .out_2(buttondetector_1_out_2));
  Multiplexer #(.width(8)) multiplexer_1 (
    .in0(Multiplier), .in1(twoscomplement_1_out_2), .out(multiplexer_1_out), .sel(Multiplier[7]));
  xor xor_1 (Sign, Multiplier[7], Multiplicand[7]);
  Multiplexer #(.width(8)) multiplexer_2 (
    .in0(Multiplicand), .in1(twoscomplement_2_out_2), .out(multiplexer_2_out), .sel(Multiplicand[7]));
  // Shift_Register shift_register_1: pin names not known; wires that end beside it: shift_register_1_p1, 1'b0, shift_register_1_p1, buttondetector_1_out_2, shift_register_1_p5, clk, 1'b0, multiplexer_1_out[7], multiplexer_1_out[6], multiplexer_1_out[5], multiplexer_1_out[4], multiplexer_1_out[3], multiplexer_1_out[2], shift_register_1_p14, shift_register_1_p14, shift_register_1_p16, shift_register_1_p17, shift_register_1_p18, shift_register_1_p19, shift_register_1_p20
  not not_1 (shift_register_1_p5, EndMult);
  // Shift_Register #(.length(15)) shift_register_2: pin names not known; wires that end beside it: multiplexer_1_out[1], multiplexer_1_out[0], shift_register_1_p1, buttondetector_1_out_2, shift_register_1_p5, clk, 1'b0, multiplexer_2_out[0], multiplexer_2_out[1], multiplexer_2_out[2], multiplexer_2_out[3], multiplexer_2_out[4], multiplexer_2_out[5], multiplexer_2_out[6], multiplexer_2_out[7], shift_register_2_p16, shift_register_2_p17, shift_register_2_p18, shift_register_2_p19[0], shift_register_2_p19[1], shift_register_2_p19[2], shift_register_2_p19[3], shift_register_2_p19[4], shift_register_2_p19[5], shift_register_2_p19[6], shift_register_2_p19[7], shift_register_2_p19[8], shift_register_2_p19[9], shift_register_2_p19[10], shift_register_2_p19[11]
  nor nor_1 (EndMult, shift_register_2_p18, shift_register_2_p17, shift_register_2_p16, shift_register_1_p20, shift_register_1_p19, shift_register_1_p18, shift_register_1_p17, shift_register_1_p16);
  Multiplexer #(.width(15)) multiplexer_3 (
    .in0({15{1'b0}}), .in1(shift_register_2_p19), .out(multiplexer_3_out), .sel(shift_register_2_p18));
  Adder #(.width(15)) adder_1 (.a(register_1_q), .b(multiplexer_3_out), .out(adder_1_out));  // open: cin, cout
  Register #(.width(15)) register_1 (
    .D(adder_1_out), .en(1'b1), .clk(clk), .Q(register_1_q), .clr(buttondetector_1_out_2));
  Multiplexer #(.width(15)) multiplexer_4 (.in0({15{1'b0}}), .in1(register_1_q), .out(Product), .sel(EndMult));
endmodule
